// Digital circuit CPU.dig as structural Verilog
module CPU (
  input  [7:0] M,
  input  [7:0] N,
  input  [12:0] progIN,
  input  reset,
  input  progLoad,
  input  start,
  input  result,
  input  clk,
  input  in_18,
  output valid,
  output done,
  output [7:0] \output ,
  output [7:0] out_12,
  output [7:0] out_13,
  output [7:0] out_14,
  output [7:0] out_15,
  output [7:0] out_16,
  output [7:0] out_17,
  output [15:0] out_19,
  output [15:0] out_20
);

  wire _10111_eq, and_1_out, and_2_out, and_3_out, and_4_out, and_5_out, and_6_out, and_7_out, and_8_out,
       and_9_out, and_10_out, and_11_out, and_12_out, and_13_out, and_14_out, and_17_out, and_18_out,
       and_19_out, and_20_out, and_21_out, and_22_out, and_23_out, and_24_out, and_26_out, and_27_out,
       and_28_out, and_29_out, and_30_out, and_31_out, and_32_out, and_33_out, and_34_out, and_35_out,
       and_36_out, and_37_out, and_38_out, and_39_out, and_40_out, and_41_out, and_42_out, and_43_out,
       and_44_out, and_45_out, and_46_out, and_47_out, and_48_out, and_49_out, and_50_out, and_51_out,
       and_52_out, ChkPrime_d, comparator_1_eq, comparator_2_eq, comparator_2_gt, comparator_2_lt,
       comparator_3_eq, comparator_4_eq, comparator_6_eq, comparator_7_eq, comparator_8_eq, comparator_9_eq,
       compare_eq, compare_gt, compare_lt, d_ff_1_q, d_ff_3_q, d_ff_6_q, d_ff_8_q, d_ff_9_q, EQ, Fstop, GT,
       JumpOn, LT, not_1_out, not_2_out, or_1_out, or_2_out, or_3_out, or_4_out, or_5_out, or_6_out,
       or_7_out, or_8_out, or_9_out, or_10_out, or_12_out, or_13_out, or_14_out, or_16_out, or_17_out,
       or_18_out, or_19_out, or_20_out, or_22_out, or_25_out, or_26_out, or_27_out, or_28_out, or_29_out,
       or_30_out, or_31_out, or_36_out, or_37_out, or_38_out, or_39_out, Prime, PrimeOn, resetDone, resetOn,
       rs_ff_as_2_q, rs_ff_as_3_q, rs_ff_as_4_q, rs_ff_as_21_q, rs_ff_as_22_q, rs_ff_as_24_q, rs_ff_as_25_q,
       rs_ff_as_26_nq, rs_ff_as_26_q, rs_ff_as_27_nq, rs_ff_as_27_q, rs_ff_as_28_q, rs_ff_as_29_q,
       rs_ff_as_30_q, t_ff_1_nq;
  wire [0:0] rs_ff_as_1_q;
  wire [3:0] counter_1_out;
  wire [4:0] out;
  wire [7:0] _00000, _00001, _2A, _00010, _00011, _00100, _00101, _00110, _00111, _01000, _01010,
       _01010_to_accA, _01011, _01100, _01101, _01110, _01111, _10000, _10001, _10001_s, _10001_to_accA,
       _10010, _10010_to_accA, _10011, _10011_to_accA, _10100, _10100_to_accA, _10101, _10101_to_accA,
       _10110, _10110_to_accA, _10111, _11000, _11001, _11001_to_accA, _11010, _11010_to_accA, _11011,
       _11011_to_accA, _11100, _11100_to_accA, _11101, _11110, _11111, add_1_s, AMore_s, Bit_shift_out,
       BMore_s, count2, counter_3_out, counter_4_out, d_ff_2_q, d_ff_4_q, d_ff_5_q, d_ff_11_q, Data_Out,
       DeleteAdr, demultiplexer_1_out_1, demultiplexer_2_out_1, demultiplexer_4_out_0, iterate, JumpPath,
       multiplexer_1_out, multiplexer_2_out, multiplexer_3_out, multiplexer_4_out, multiplexer_5_out,
       multiplexer_6_out, multiplexer_7_out, multiplexer_8_out, multiplexer_9_out, multiplexer_10_out,
       multiplexer_11_out, multiplexer_13_out, multiplexer_15_out, multiplexer_16_out, multiplexer_17_out,
       multiplexer_18_out, multiplexer_19_out, multiplexer_20_out, multiplexer_21_out, multiplexer_22_out,
       multiplexer_23_out, multiplexer_24_out, multiplexer_25_out, multiplexer_26_out, multiplexer_29_out,
       multiplexer_30_out, multiplexer_31_out, multiplexer_32_out, multiplexer_33_out, multiplexer_34_out,
       multiplexer_35_out, multiplexer_36_out, multiplexer_37_out, multiplexer_38_out, multiplexer_39_out,
       multiplexer_40_out, multiplexer_41_out, multiplexer_42_out, multiplexer_43_out, multiplexer_44_out,
       OppositeA, or_21_out, or_24_out, or_32_out, or_33_out, or_34_out, or_35_out, rRam_d1, rRam_d2;
  wire [12:0] _2D, d_ff_7_q, pRAM_d1;
  wire [15:0] mul_1_mul, rs_ff_as_20_q;

  D_FF d_ff_1 (.D(or_3_out), .C(clk), .Q(d_ff_1_q));  // open: nQ
  Multiplexer #(.Bits(8)) multiplexer_1 (.sel(rs_ff_as_3_q), .in_0(_01011), .in_1(iterate), .out(multiplexer_1_out));
  Multiplexer #(.Bits(8)) multiplexer_2 (.sel(rs_ff_as_2_q), .in_0(out_13), .in_1({8{1'b0}}), .out(multiplexer_2_out));
  RS_FF_AS rs_ff_as_1 (.S(d_ff_1_q), .R(reset), .Q(rs_ff_as_1_q[0]));  // open: nQ
  Comparator #(.Bits(5)) comparator_1 (.a(out), .b(5'b01011), .eq(comparator_1_eq));  // open: gt, lt
  Multiplexer #(.Bits(8)) multiplexer_3 (
    .sel(rs_ff_as_2_q), .in_0(multiplexer_1_out), .in_1(DeleteAdr), .out(multiplexer_3_out));
  RS_FF_AS rs_ff_as_2 (.S(resetOn), .R(resetDone), .Q(rs_ff_as_2_q));  // open: nQ
  Multiplexer #(.Bits(8)) multiplexer_4 (
    .sel(or_3_out), .in_0(multiplexer_2_out), .in_1(multiplexer_13_out), .out(multiplexer_4_out));
  Add #(.Bits(8)) add_1 (.a(8'he), .b({{7{1'b0}}, rs_ff_as_1_q[0]}), .c_i(1'b0), .s(add_1_s));  // open: c_o
  RS_FF_AS rs_ff_as_3 (.S(result), .R(reset), .Q(rs_ff_as_3_q));  // open: nQ
  D_FF #(.Bits(8)) d_ff_2 (.D(add_1_s), .C(~clk), .Q(d_ff_2_q));  // open: nQ
  or or_1 (or_1_out, comparator_1_eq, or_3_out, resetOn);
  Multiplexer #(.Bits(8)) multiplexer_5 (
    .sel(and_1_out), .in_0(multiplexer_3_out), .in_1({4'b0000, _11110[3:0]}), .out(multiplexer_5_out));
  Multiplexer #(.Bits(8)) multiplexer_6 (
    .sel(or_3_out), .in_0(multiplexer_5_out), .in_1(d_ff_2_q), .out(multiplexer_6_out));
  Multiplexer #(.Bits(8)) multiplexer_7 (
    .sel(and_1_out), .in_0(_01010), .in_1({4'b0000, _11110[7:4]}), .out(multiplexer_7_out));
  RAMDualAccess #(.AddrBits(8), .Bits(8)) rRam (
    .str(or_1_out), .C(clk), .ld(1'b1), .A1(multiplexer_6_out), .Din1(multiplexer_4_out),
    .A2(multiplexer_7_out), .D1(rRam_d1), .D2(rRam_d2));
  and and_1 (and_1_out, ~out[0], out[1], out[2], out[3], out[4]);  // And
  Demultiplexer #(.Bits(8)) demultiplexer_1 (
    .sel(and_1_out), .in(rRam_d1), .out_0(Data_Out), .out_1(demultiplexer_1_out_1));
  Demultiplexer #(.Bits(8)) demultiplexer_2 (
    .sel(and_1_out), .in(rRam_d2), .out_0(_01010_to_accA), .out_1(demultiplexer_2_out_1));
  Mul #(.Bits(8)) mul_1 (.a(demultiplexer_1_out_1), .b(demultiplexer_2_out_1), .mul(mul_1_mul));
  RS_FF_AS rs_ff_as_4 (.S(and_1_out), .R(reset), .Q(rs_ff_as_4_q));  // open: nQ
  D_FF d_ff_3 (.D(rs_ff_as_4_q), .C(clk), .Q(d_ff_3_q));  // open: nQ
  Multiplexer #(.Bits(8)) multiplexer_8 (
    .sel(d_ff_3_q), .in_0(demultiplexer_1_out_1), .in_1(multiplexer_10_out), .out(multiplexer_8_out));
  Multiplexer #(.Bits(8)) multiplexer_9 (
    .sel(d_ff_3_q), .in_0(demultiplexer_2_out_1), .in_1(multiplexer_11_out), .out(multiplexer_9_out));
  D_FF #(.Bits(8)) d_ff_4 (.D(multiplexer_8_out), .C(clk), .Q(d_ff_4_q));  // open: nQ
  D_FF #(.Bits(8)) d_ff_5 (.D(multiplexer_9_out), .C(clk), .Q(d_ff_5_q));  // open: nQ
  Comparator #(.Bits(8)) comparator_2 (
    .a(d_ff_4_q), .b(d_ff_5_q), .gt(comparator_2_gt), .eq(comparator_2_eq), .lt(comparator_2_lt));
  Sub #(.Bits(8)) AMore (.a(d_ff_4_q), .b(d_ff_5_q), .c_i(1'b0), .s(AMore_s));  // open: c_o
  Sub #(.Bits(8)) BMore (.a(d_ff_5_q), .b(d_ff_4_q), .c_i(1'b0), .s(BMore_s));  // open: c_o
  Multiplexer #(.Bits(8)) multiplexer_10 (
    .sel(comparator_2_gt), .in_0(d_ff_4_q), .in_1(AMore_s), .out(multiplexer_10_out));
  Multiplexer #(.Bits(8)) multiplexer_11 (
    .sel(comparator_2_lt), .in_0(d_ff_5_q), .in_1(BMore_s), .out(multiplexer_11_out));
  RS_FF_AS rs_ff_as_5 (.S(mul_1_mul[0]), .R(reset), .Q(rs_ff_as_20_q[0]));  // open: nQ
  RS_FF_AS rs_ff_as_6 (.S(mul_1_mul[1]), .R(reset), .Q(rs_ff_as_20_q[1]));  // open: nQ
  RS_FF_AS rs_ff_as_7 (.S(mul_1_mul[2]), .R(reset), .Q(rs_ff_as_20_q[2]));  // open: nQ
  RS_FF_AS rs_ff_as_8 (.S(mul_1_mul[3]), .R(reset), .Q(rs_ff_as_20_q[3]));  // open: nQ
  RS_FF_AS rs_ff_as_9 (.S(mul_1_mul[4]), .R(reset), .Q(rs_ff_as_20_q[4]));  // open: nQ
  RS_FF_AS rs_ff_as_10 (.S(mul_1_mul[5]), .R(reset), .Q(rs_ff_as_20_q[5]));  // open: nQ
  RS_FF_AS rs_ff_as_11 (.S(mul_1_mul[6]), .R(reset), .Q(rs_ff_as_20_q[6]));  // open: nQ
  RS_FF_AS rs_ff_as_12 (.S(mul_1_mul[7]), .R(reset), .Q(rs_ff_as_20_q[7]));  // open: nQ
  RS_FF_AS rs_ff_as_13 (.S(mul_1_mul[8]), .R(reset), .Q(rs_ff_as_20_q[8]));  // open: nQ
  RS_FF_AS rs_ff_as_14 (.S(mul_1_mul[9]), .R(reset), .Q(rs_ff_as_20_q[9]));  // open: nQ
  RS_FF_AS rs_ff_as_15 (.S(mul_1_mul[10]), .R(reset), .Q(rs_ff_as_20_q[10]));  // open: nQ
  RS_FF_AS rs_ff_as_16 (.S(mul_1_mul[11]), .R(reset), .Q(rs_ff_as_20_q[11]));  // open: nQ
  RS_FF_AS rs_ff_as_17 (.S(mul_1_mul[12]), .R(reset), .Q(rs_ff_as_20_q[12]));  // open: nQ
  RS_FF_AS rs_ff_as_18 (.S(mul_1_mul[13]), .R(reset), .Q(rs_ff_as_20_q[13]));  // open: nQ
  RS_FF_AS rs_ff_as_19 (.S(mul_1_mul[14]), .R(reset), .Q(rs_ff_as_20_q[14]));  // open: nQ
  RS_FF_AS rs_ff_as_20 (.S(mul_1_mul[15]), .R(reset), .Q(rs_ff_as_20_q[15]));  // open: nQ
  Multiplexer #(.Bits(8)) multiplexer_12 (.sel(comparator_2_eq), .in_0({8{1'b0}}), .in_1(d_ff_4_q), .out(out_20[7:0]));
  or or_2 (or_2_out, comparator_4_eq, reset);
  RS_FF_AS rs_ff_as_21 (.S(and_1_out), .R(or_2_out), .Q(rs_ff_as_21_q));  // open: nQ
  Div #(.Bits(16)) div_1 (.a(rs_ff_as_20_q), .b({{8{1'b0}}, out_20[7:0]}), .q(out_19));  // open: r
  Counter #(.Bits(4)) counter_1 (.en(rs_ff_as_21_q), .C(clk), .clr(or_2_out), .out(counter_1_out));  // open: ovf
  Comparator #(.Bits(4)) comparator_3 (.a(counter_1_out), .b(4'b1100), .eq(comparator_3_eq));  // open: gt, lt
  or or_3 (or_3_out, comparator_4_eq, comparator_3_eq);
  T_FF t_ff_1 (.T(1'b1), .C(clk), .nQ(t_ff_1_nq));  // open: Q
  Comparator #(.Bits(4)) comparator_4 (.a(counter_1_out), .b(4'b1101), .eq(comparator_4_eq));  // open: gt, lt
  Multiplexer #(.Bits(8)) multiplexer_13 (
    .sel(t_ff_1_nq), .in_0(out_19[7:0]), .in_1(out_19[15:8]), .out(multiplexer_13_out));
  RS_FF_AS rs_ff_as_22 (.S(result), .R(reset), .Q(rs_ff_as_22_q));  // open: nQ
  Multiplexer #(.Bits(8)) multiplexer_14 (.sel(rs_ff_as_22_q), .in_0({8{1'b0}}), .in_1(Data_Out), .out(\output ));
  and and_2 (and_2_out, rs_ff_as_24_q, reset);
  RS_FF_AS rs_ff_as_23 (.S(and_2_out), .R(resetDone), .Q(resetOn));  // open: nQ
  or or_4 (or_4_out, reset, resetDone);
  Seven_Seg_Hex seven_seg_hex_1 (.d(\output [7:4]), .dp(1'b0));
  RS_FF_AS rs_ff_as_24 (.S(start), .R(resetDone), .Q(rs_ff_as_24_q));  // open: nQ
  Counter #(.Bits(8)) counter_2 (.en(resetOn), .C(clk), .clr(or_4_out), .out(DeleteAdr));  // open: ovf
  Seven_Seg_Hex seven_seg_hex_2 (.d(\output [3:0]), .dp(1'b0));
  // Probe on DeleteAdr
  Comparator #(.Bits(8)) comparator_5 (.a(DeleteAdr), .b(8'hf), .eq(resetDone));  // open: gt, lt
  D_FF d_ff_6 (.D(reset), .C(clk), .Q(d_ff_6_q));  // open: nQ
  or or_5 (or_5_out, d_ff_6_q, rs_ff_as_25_q);
  RS_FF_AS rs_ff_as_25 (.S(or_6_out), .R(or_9_out), .Q(rs_ff_as_25_q));  // open: nQ
  or or_6 (or_6_out, JumpOn, start);
  and and_3 (and_3_out, ~out[4], out[3], out[2], ~out[1], ~out[0]);  // And
  and and_4 (and_4_out, ~out[4], out[3], out[2], ~out[1], out[0]);  // And
  and and_5 (and_5_out, ~out[4], out[3], out[2], out[1], ~out[0]);  // And
  and and_6 (and_6_out, ~out[4], out[3], out[2], out[1], out[0]);  // And
  and and_7 (and_7_out, out[4], ~out[3], ~out[2], ~out[1], ~out[0]);  // And
  or or_7 (or_7_out, EQ, GT);
  Multiplexer #(.Bits(8)) multiplexer_15 (.sel(rs_ff_as_26_q), .in_0(out_16), .in_1(count2), .out(multiplexer_15_out));
  LED led_1 (.in(rs_ff_as_26_nq));
  RS_FF_AS rs_ff_as_26 (.S(start), .R(or_10_out), .Q(rs_ff_as_26_q), .nQ(rs_ff_as_26_nq));
  not not_1 (not_1_out, clk);
  or or_8 (or_8_out, clk, d_ff_6_q);
  or or_9 (or_9_out, reset, and_13_out);
  or or_10 (or_10_out, reset, progLoad);
  RS_FF_AS rs_ff_as_27 (.S(progLoad), .R(not_1_out), .Q(rs_ff_as_27_q), .nQ(rs_ff_as_27_nq));
  and and_8 (and_8_out, ~in_18, or_8_out);  // And
  CounterPreset #(.Bits(8)) counterpreset_1 (
    .en(or_5_out), .C(and_8_out), .dir(1'b0), .in(JumpPath), .ld(JumpOn), .clr(d_ff_6_q), .out(count2));  // open: ovf
  and and_9 (and_9_out, and_4_out, EQ);
  and and_10 (and_10_out, and_5_out, GT);
  and and_11 (and_11_out, and_6_out, LT);
  and and_12 (and_12_out, and_7_out, or_7_out);
  RS_FF_AS rs_ff_as_28 (.S(start), .R(reset), .Q(rs_ff_as_28_q));  // open: nQ
  RAMDualAccess #(.AddrBits(8), .Bits(13)) pRAM (
    .str(progLoad), .C(clk), .ld(1'b1), .A1(multiplexer_15_out), .Din1(d_ff_7_q), .A2(_2A), .D1(pRAM_d1),
    .D2(_2D));
  or or_11 (JumpOn, and_3_out, and_9_out, and_10_out, and_11_out, and_12_out);
  Multiplexer #(.Bits(13)) multiplexer_16 (
    .sel(rs_ff_as_28_q), .in_0({13{1'b0}}), .in_1(pRAM_d1), .out({out, multiplexer_16_out}));
  // Probe on _2D
  D_FF #(.Bits(13)) d_ff_7 (.D(progIN), .C(~clk), .Q(d_ff_7_q));  // open: nQ
  or or_12 (or_12_out, rs_ff_as_27_q, reset);
  Comparator #(.Bits(8)) comparator_6 (.a(out_16), .b({8{1'b0}}), .eq(comparator_6_eq));  // open: gt, lt
  // Probe on count2
  // Probe on {out, multiplexer_16_out}
  // Probe on out
  RS_FF_AS rs_ff_as_29 (.S(start), .R(reset), .Q(rs_ff_as_29_q));  // open: nQ
  and and_13 (and_13_out, ~JumpOn, or_13_out);  // And
  Multiplexer #(.Bits(8)) multiplexer_17 (.sel(and_3_out), .in_0({8{1'b0}}), .in_1(_01100), .out(multiplexer_17_out));
  Multiplexer #(.Bits(8)) multiplexer_18 (.sel(and_9_out), .in_0({8{1'b0}}), .in_1(_01101), .out(multiplexer_18_out));
  Multiplexer #(.Bits(8)) multiplexer_19 (.sel(and_10_out), .in_0({8{1'b0}}), .in_1(_01110), .out(multiplexer_19_out));
  Multiplexer #(.Bits(8)) multiplexer_20 (.sel(and_11_out), .in_0({8{1'b0}}), .in_1(_01111), .out(multiplexer_20_out));
  Multiplexer #(.Bits(8)) multiplexer_21 (.sel(and_12_out), .in_0({8{1'b0}}), .in_1(_10000), .out(multiplexer_21_out));
  Demultiplexer #(.Selector_Bits(5), .Bits(8)) demultiplexer_3 (
    .sel(out), .in(multiplexer_16_out), .out_0(_00000), .out_1(_00001), .out_2(_00010), .out_3(_00011),
    .out_4(_00100), .out_5(_00101), .out_6(_00110), .out_7(_00111), .out_8(_01000), .out_9(_2A),
    .out_10(_01010), .out_11(_01011), .out_12(_01100), .out_13(_01101), .out_14(_01110), .out_15(_01111),
    .out_16(_10000), .out_17(_10001), .out_18(_10010), .out_19(_10011), .out_20(_10100), .out_21(_10101),
    .out_22(_10110), .out_23(_10111), .out_24(_11000), .out_25(_11001), .out_26(_11010), .out_27(_11011),
    .out_28(_11100), .out_29(_11101), .out_30(_11110), .out_31(_11111));
  Counter #(.Bits(8)) counter_3 (.en(1'b1), .C(or_12_out), .clr(reset), .out(counter_3_out));  // open: ovf
  and and_14 (and_14_out, rs_ff_as_29_q, Fstop);
  or or_13 (or_13_out, comparator_6_eq, Fstop);
  Sub #(.Bits(8)) sub_1 (.a(counter_3_out), .b(8'h1), .c_i(1'b0), .s(out_16));  // open: c_o
  or or_14 (or_14_out, Fstop, and_14_out);
  assign JumpPath = multiplexer_17_out | multiplexer_18_out | multiplexer_19_out | multiplexer_20_out | multiplexer_21_out;  // Or or_15, 8 bits wide
  and and_15 (valid, or_14_out, ~start);  // And
  // Probe on out_16
  and and_16 (Fstop, rs_ff_as_29_q, out[0], out[1], out[2], out[3], out[4]);
  and and_17 (and_17_out, result, valid);
  D_FF d_ff_8 (.D(and_17_out), .C(clk), .Q(d_ff_8_q));  // open: nQ
  D_FF d_ff_9 (.D(d_ff_8_q), .C(clk), .Q(d_ff_9_q));  // open: nQ
  Add #(.Bits(8)) u__10001 (.a(out_13), .b(out_14), .c_i(1'b0), .s(_10001_s));  // open: c_o
  Sub #(.Bits(8)) u__10010 (.a(out_13), .b(out_14), .c_i(1'b0), .s(_10010_to_accA));  // open: c_o
  Mul #(.Bits(4)) u__10011 (.a(out_13[3:0]), .b(out_14[3:0]), .mul(_10011_to_accA));
  Div #(.Bits(8)) u__10100 (.a(out_13), .b(out_14), .q(_10100_to_accA), .r(_10101_to_accA));
  ROM #(.AddrBits(6), .Bits(8)) Power (.A({out_13[2:0], out_14[2:0]}), .sel(1'b1), .D(_10110_to_accA));
  RS_FF_AS rs_ff_as_30 (.S(d_ff_9_q), .R(or_16_out), .Q(rs_ff_as_30_q));  // open: nQ
  // Probe on _2D[12:8]
  and and_18 (and_18_out, clk, rs_ff_as_30_q);
  D_FF #(.Bits(8)) d_ff_10 (.D(_10001_s), .C(clk), .Q(_10001_to_accA));  // open: nQ
  and and_19 (and_19_out, clk, ~out[0], out[1], ~out[2], ~out[3], ~out[4]);  // And
  and and_20 (and_20_out, clk, ~out[0], ~out[1], out[2], ~out[3], ~out[4]);  // And
  or or_16 (or_16_out, reset, comparator_7_eq);
  or or_17 (or_17_out, and_18_out, and_28_out);
  or or_18 (or_18_out, reset, ~comparator_7_eq, and_28_out);  // Or
  Multiplexer #(.Bits(8)) multiplexer_22 (.sel(and_19_out), .in_0({8{1'b0}}), .in_1(_00010), .out(multiplexer_22_out));
  Multiplexer #(.Bits(8)) multiplexer_23 (.sel(and_20_out), .in_0({8{1'b0}}), .in_1(out_13), .out(multiplexer_23_out));
  or or_19 (or_19_out, and_20_out, and_19_out);
  and and_21 (and_21_out, ~out[4], ~out[3], out[2], ~out[1], out[0]);  // And
  and and_22 (and_22_out, ~out[4], ~out[3], out[2], out[1], out[0]);  // And
  and and_23 (and_23_out, ~out[4], out[3], ~out[2], ~out[1], ~out[0]);  // And
  or or_20 (or_20_out, or_17_out, reset, comparator_7_eq);
  assign or_21_out = multiplexer_22_out | multiplexer_23_out;  // Or or_21, 8 bits wide
  or or_22 (or_22_out, reset, comparator_7_eq);
  and and_24 (and_24_out, clk, or_19_out);
  Multiplexer #(.Bits(8)) multiplexer_24 (.sel(and_21_out), .in_0({8{1'b0}}), .in_1(out_13), .out(multiplexer_24_out));
  Multiplexer #(.Bits(8)) multiplexer_25 (.sel(and_22_out), .in_0({8{1'b0}}), .in_1(M), .out(multiplexer_25_out));
  Multiplexer #(.Bits(8)) multiplexer_26 (.sel(and_23_out), .in_0({8{1'b0}}), .in_1(N), .out(multiplexer_26_out));
  Counter #(.Bits(8)) counter_4 (.en(1'b1), .C(or_20_out), .clr(or_22_out), .out(counter_4_out));  // open: ovf
  RS_FF_AS rs_ff_as_31 (.S(comparator_7_eq), .R(or_18_out), .Q(done));  // open: nQ
  Comparator #(.Bits(5)) u__10111 (.a(out), .b(5'b10111), .eq(_10111_eq));  // open: gt, lt
  assign _11001_to_accA = out_13 & out_14;  // And and_25, 8 bits wide
  assign _11010_to_accA = out_13 | out_14;  // Or or_23, 8 bits wide
  assign _11011_to_accA = out_13 ^ out_14;  // XOr xor_1, 8 bits wide
  assign or_24_out = multiplexer_24_out | multiplexer_25_out | multiplexer_26_out;  // Or or_24, 8 bits wide
  or or_25 (or_25_out, and_23_out, and_22_out, and_21_out);
  Comparator #(.Bits(8)) compare (.a(out_13), .b(out_14), .gt(compare_gt), .eq(compare_eq), .lt(compare_lt));
  BarrelShifter #(.Bits(8)) Bit_shift (.in(out_13), .shift({1'b0, out_14[2:0]}), .out(Bit_shift_out));
  D_FF_AS #(.Bits(8)) accB (.Set(1'b0), .D(or_21_out), .C(and_24_out), .Clr(reset), .Q(out_14));  // open: nQ
  and and_26 (and_26_out, or_25_out, clk);
  Multiplexer #(.Bits(8)) multiplexer_27 (.sel(or_27_out), .in_0(counter_4_out), .in_1({8{1'b0}}), .out(iterate));
  and and_27 (and_27_out, compare_gt, _10111_eq);
  RS_FF_AS rs_ff_as_32 (.S(and_27_out), .R(and_29_out), .Q(GT));  // open: nQ
  D_FF #(.Bits(8)) d_ff_11 (.D(Bit_shift_out), .C(comparator_8_eq), .Q(d_ff_11_q));  // open: nQ
  D_FF_AS #(.Bits(8)) regC (.Set(1'b0), .D(or_24_out), .C(and_26_out), .Clr(reset), .Q(out_12));  // open: nQ
  // Probe on iterate
  Comparator #(.Bits(8)) comparator_7 (.a(iterate), .b(8'h10), .eq(comparator_7_eq));  // open: gt, lt
  and and_28 (and_28_out, result, comparator_7_eq);
  or or_26 (or_26_out, compare_eq, compare_lt);
  and and_29 (and_29_out, _10111_eq, or_26_out);
  Demultiplexer #(.Bits(8)) demultiplexer_4 (
    .sel(comparator_8_eq), .in(d_ff_11_q), .out_0(demultiplexer_4_out_0), .out_1(_11100_to_accA));
  or or_27 (or_27_out, reset, and_28_out);
  and and_30 (and_30_out, compare_eq, _10111_eq);
  and and_31 (and_31_out, Prime, PrimeOn);
  or or_28 (or_28_out, and_30_out, and_31_out);
  Comparator #(.Bits(5)) comparator_8 (.a(out), .b(5'b11100), .eq(comparator_8_eq));  // open: gt, lt
  or or_29 (or_29_out, compare_gt, compare_lt);
  and and_32 (and_32_out, _10111_eq, or_29_out);
  or or_30 (or_30_out, and_33_out, and_32_out);
  RS_FF_AS rs_ff_as_33 (.S(or_28_out), .R(or_30_out), .Q(EQ));  // open: nQ
  not not_2 (not_2_out, Prime);
  and and_33 (and_33_out, not_2_out, PrimeOn);
  Comparator #(.Bits(5)) primeSW (.a(out), .b(5'b11101), .eq(PrimeOn));  // open: gt, lt
  ROM #(.AddrBits(8)) ChkPrime (.A(out_13), .sel(1'b1), .D(ChkPrime_d));
  and and_34 (and_34_out, compare_lt, _10111_eq);
  RS_FF_AS rs_ff_as_34 (.S(and_34_out), .R(and_35_out), .Q(LT));  // open: nQ
  Multiplexer multiplexer_28 (.sel(comparator_9_eq), .in_0(1'b0), .in_1(ChkPrime_d), .out(Prime));
  Comparator #(.Bits(5)) comparator_9 (.a(out), .b(5'b11101), .eq(comparator_9_eq));  // open: gt, lt
  or or_31 (or_31_out, compare_gt, compare_eq);
  and and_35 (and_35_out, _10111_eq, or_31_out);
  and and_36 (and_36_out, ~out[4], ~out[3], ~out[2], ~out[1], out[0]);  // And
  and and_37 (and_37_out, ~out[4], ~out[3], ~out[2], out[1], out[0]);  // And
  and and_38 (and_38_out, ~out[4], ~out[3], out[2], out[1], ~out[0]);  // And
  and and_39 (and_39_out, ~out[4], out[3], ~out[2], ~out[1], out[0]);  // And
  and and_40 (and_40_out, ~out[4], out[3], ~out[2], out[1], ~out[0]);  // And
  and and_41 (and_41_out, out[4], ~out[3], ~out[2], ~out[1], out[0]);  // And
  and and_42 (and_42_out, out[4], ~out[3], ~out[2], out[1], ~out[0]);  // And
  and and_43 (and_43_out, out[4], ~out[3], ~out[2], out[1], out[0]);  // And
  and and_44 (and_44_out, out[4], ~out[3], out[2], ~out[1], ~out[0]);  // And
  and and_45 (and_45_out, out[4], ~out[3], out[2], ~out[1], out[0]);  // And
  and and_46 (and_46_out, out[4], ~out[3], out[2], out[1], ~out[0]);  // And
  and and_47 (and_47_out, out[4], out[3], ~out[2], ~out[1], ~out[0]);  // And
  and and_48 (and_48_out, out[4], out[3], ~out[2], ~out[1], out[0]);  // And
  and and_49 (and_49_out, out[4], out[3], ~out[2], out[1], ~out[0]);  // And
  and and_50 (and_50_out, out[4], out[3], ~out[2], out[1], out[0]);  // And
  and and_51 (and_51_out, out[4], out[3], out[2], ~out[1], ~out[0]);  // And
  assign or_32_out = multiplexer_29_out | multiplexer_30_out | multiplexer_31_out | multiplexer_32_out | multiplexer_33_out;  // Or or_32, 8 bits wide
  Multiplexer #(.Bits(8)) multiplexer_29 (.sel(and_36_out), .in_0({8{1'b0}}), .in_1(_00001), .out(multiplexer_29_out));
  Multiplexer #(.Bits(8)) multiplexer_30 (.sel(and_37_out), .in_0({8{1'b0}}), .in_1(out_14), .out(multiplexer_30_out));
  Multiplexer #(.Bits(8)) multiplexer_31 (.sel(and_38_out), .in_0({8{1'b0}}), .in_1(out_12), .out(multiplexer_31_out));
  Multiplexer #(.Bits(8)) multiplexer_32 (
    .sel(and_39_out), .in_0({8{1'b0}}), .in_1(_2D[7:0]), .out(multiplexer_32_out));
  Multiplexer #(.Bits(8)) multiplexer_33 (
    .sel(and_40_out), .in_0({8{1'b0}}), .in_1(_01010_to_accA), .out(multiplexer_33_out));
  Multiplexer #(.Bits(8)) multiplexer_34 (
    .sel(and_41_out), .in_0({8{1'b0}}), .in_1(_10001_to_accA), .out(multiplexer_34_out));
  Multiplexer #(.Bits(8)) multiplexer_35 (
    .sel(and_42_out), .in_0({8{1'b0}}), .in_1(_10010_to_accA), .out(multiplexer_35_out));
  Multiplexer #(.Bits(8)) multiplexer_36 (
    .sel(and_43_out), .in_0({8{1'b0}}), .in_1(_10011_to_accA), .out(multiplexer_36_out));
  Multiplexer #(.Bits(8)) multiplexer_37 (
    .sel(and_44_out), .in_0({8{1'b0}}), .in_1(_10100_to_accA), .out(multiplexer_37_out));
  Multiplexer #(.Bits(8)) multiplexer_38 (
    .sel(and_45_out), .in_0({8{1'b0}}), .in_1(_10101_to_accA), .out(multiplexer_38_out));
  Multiplexer #(.Bits(8)) multiplexer_39 (
    .sel(and_46_out), .in_0({8{1'b0}}), .in_1(_10110_to_accA), .out(multiplexer_39_out));
  Multiplexer #(.Bits(8)) multiplexer_40 (
    .sel(and_47_out), .in_0({8{1'b0}}), .in_1(OppositeA), .out(multiplexer_40_out));
  Multiplexer #(.Bits(8)) multiplexer_41 (
    .sel(and_48_out), .in_0({8{1'b0}}), .in_1(_11001_to_accA), .out(multiplexer_41_out));
  Multiplexer #(.Bits(8)) multiplexer_42 (
    .sel(and_49_out), .in_0({8{1'b0}}), .in_1(_11010_to_accA), .out(multiplexer_42_out));
  Multiplexer #(.Bits(8)) multiplexer_43 (
    .sel(and_50_out), .in_0({8{1'b0}}), .in_1(_11011_to_accA), .out(multiplexer_43_out));
  Multiplexer #(.Bits(8)) multiplexer_44 (
    .sel(and_51_out), .in_0({8{1'b0}}), .in_1(_11100_to_accA), .out(multiplexer_44_out));
  assign or_33_out = multiplexer_34_out | multiplexer_35_out | multiplexer_36_out | multiplexer_37_out | multiplexer_38_out;  // Or or_33, 8 bits wide
  assign or_34_out = or_32_out | or_33_out | or_35_out | multiplexer_44_out;  // Or or_34, 8 bits wide
  assign or_35_out = multiplexer_39_out | multiplexer_40_out | multiplexer_41_out | multiplexer_42_out | multiplexer_43_out;  // Or or_35, 8 bits wide
  or or_36 (or_36_out, and_36_out, and_37_out, and_38_out, and_39_out, and_40_out);
  or or_37 (or_37_out, and_41_out, and_42_out, and_43_out, and_44_out, and_45_out);
  or or_38 (or_38_out, and_46_out, and_47_out, and_48_out, and_49_out, and_50_out);
  or or_39 (or_39_out, or_36_out, or_37_out, or_38_out, and_51_out);
  and and_52 (and_52_out, ~clk, or_39_out);  // And
  D_FF_AS #(.Bits(8)) accA (.Set(1'b0), .D(or_34_out), .C(and_52_out), .Clr(reset), .Q(out_13), .nQ(OppositeA));

  assign out_15 = out_12;
  assign out_17 = out_16;
  assign out_20[15:8] = {8{1'b0}};

  // Other names for the same wires on the sheet: GCD[7:0] = out_20[7:0]; _01001[7:0] = _2A;
  //   _01001_to_accA[7:0] = _2D[7:0]; count[7:0] = out_16; NotDone = in_18; OA[7:0] = out_13; OB[7:0] = out_14;
  //   OC[7:0] = out_12

  // Notes on the sheet:
  //   rRam
  //   Delete Iterator
  //   Main Loop Counter
  //   Jump Check
  //   pRam
  //   ProgIn Loop
  //   ALU modules
  //   accB and regC
  //   Result Iterator
  //   pRam to accA
  //   contents of Power (hex, n*v repeats v):
  //   1,7*0,9*1,2,4,8,10,1a,40,80,1,3,9,1b,51,f3,2d9,88b,1,4,10,40,100
  //   ,400,0,0,1,5,19,7d,271,c35,3d09,1312d,1,6,24,d8,510,1e60,b640
  //   ,44580,1,7,31,157,961,41a7,1cb91,c90f7
  //   contents of ChkPrime (hex, n*v repeats v):
  //   0,0,1,1,0,1,0,1,0,0,0,1,0,1,0,0,0,1,0,1,0,0,0,1,5*0,1,0,1,5*0
  //   ,1,0,0,0,1,0,1,0,0,0,1,5*0,1,5*0,1,0,1,5*0,1,0,0,0,1,0,1,5*0,1
  //   ,0,0,0,1,5*0,1,7*0,1,0,0,0,1,0,1,0,0,0,1,0,1,0,0,0,1,13*0,1,0,0,0
  //   ,1,5*0,1,0,1,9*0,1,0,1,5*0,1,5*0,1,0,0,0,1,5*0,1,5*0,1,0,1,9*0
  //   ,1,0,1,0,0,0,1,0,1,11*0,1,11*0,1,0,0,0,1,0,1,0,0,0,1,5*0,1,0,1
  //   ,9*0,1
  //   Data accA
  //   Clock aacA
endmodule

/* Test case future:
M N progIN reset progLoad start result clk valid done output
0 0 0 0 0 0 0 0 x x x
0 0 0 0 0 0 0 1 x x x
0 0 0 1 0 0 0 0 x x x
0 0 0 1 0 0 0 1 0 0 x
0 0 0 0 0 0 0 0 0 0 x
0 0 0 0 0 0 0 1 0 0 x
0 0 0 0 0 0 0 0 0 0 x
0 0 0 0 0 0 0 1 0 0 x
0 0 0 0 0 0 0 0 0 0 x
0 0 0 0 0 0 0 1 0 0 x
0 0 0 0 0 0 0 0 0 0 x
0 0 0 0 0 0 0 1 0 0 x
0 0 0 0 0 0 0 0 0 0 x
0 0 0 0 0 0 0 1 0 0 x
0 0 0 0 0 0 0 0 0 0 x
0 0 0 0 0 0 0 1 0 0 x
0 0 0 0 0 0 0 0 0 0 x
0 0 0 0 0 0 0 1 0 0 x
0 0 0 0 0 0 0 0 0 0 x
0 0 0 0 0 0 0 1 0 0 x
0 0 0 0 0 0 0 0 0 0 x
0 0 0 0 0 0 0 1 0 0 x
0 0 0 0 0 0 0 0 0 0 x
0 0 0 0 0 0 0 1 0 0 x
0 0 0 0 0 0 0 0 0 0 x
0 0 0 0 0 0 0 1 0 0 x
0 0 0 0 0 0 0 0 0 0 x
0 0 0 0 0 0 0 1 0 0 x
0 0 0 0 0 0 0 0 0 0 x
0 0 0 0 0 0 0 1 0 0 x
0 0 0 0 0 0 0 0 0 0 x
0 0 0 0 0 0 0 1 0 0 x
0 0 0 0 0 0 0 0 0 0 x
0 0 0 0 0 0 0 1 0 0 x
0 0 0 0 0 0 0 0 0 0 x
0 0 0 0 0 0 0 1 0 0 x
0 0 0 0 0 0 0 0 0 0 x
0 0 0 0 0 0 0 1 0 0 x
0 0 0 0 0 0 0 0 0 0 x
0 0 0 0 0 0 0 1 0 0 x
0 0 0 0 0 0 0 0 0 0 x
0 0 0 0 0 0 0 1 0 0 x
0 0 276 0 1 0 0 0 0 0 x
0 0 276 0 1 0 0 1 0 0 x
0 0 2816 0 1 0 0 0 0 0 x
0 0 2816 0 1 0 0 1 0 0 x
0 0 286 0 1 0 0 0 0 0 x
0 0 286 0 1 0 0 1 0 0 x
0 0 2821 0 1 0 0 0 0 0 x
0 0 2821 0 1 0 0 1 0 0 x
0 0 7685 0 1 0 0 0 0 0 x
0 0 7685 0 1 0 0 1 0 0 x
0 0 7936 0 1 0 0 0 0 0 x
0 0 7936 0 1 0 0 1 0 0 x
0 0 0 0 0 0 0 0 0 0 x
0 0 0 0 0 0 0 1 0 0 x
0 0 0 0 0 0 0 0 0 0 x
0 0 0 0 0 0 0 1 0 0 x
0 0 0 0 0 0 0 0 0 0 x
0 0 0 0 0 0 0 1 0 0 x
0 0 0 0 0 1 0 0 x 0 x
0 0 0 0 0 1 0 1 x 0 x
0 0 0 0 0 0 0 0 x 0 x
0 0 0 0 0 0 0 1 x 0 x
0 0 0 0 0 0 0 0 x 0 x
0 0 0 0 0 0 0 1 x 0 x
0 0 0 0 0 0 0 0 x 0 x
0 0 0 0 0 0 0 1 x 0 x
0 0 0 0 0 0 0 0 x 0 x
0 0 0 0 0 0 0 1 x 0 x
0 0 0 0 0 0 0 0 x 0 x
0 0 0 0 0 0 0 1 x 0 x
0 0 0 0 0 0 0 0 x 0 x
0 0 0 0 0 0 0 1 x 0 x
0 0 0 0 0 0 0 0 x 0 x
0 0 0 0 0 0 0 1 x 0 x
0 0 0 0 0 0 0 0 x 0 x
0 0 0 0 0 0 0 1 x 0 x
0 0 0 0 0 0 0 0 x 0 x
0 0 0 0 0 0 0 1 x 0 x
0 0 0 0 0 0 0 0 x 0 x
0 0 0 0 0 0 0 1 x 0 x
0 0 0 0 0 0 0 0 x 0 x
0 0 0 0 0 0 0 1 x 0 x
0 0 0 0 0 0 0 0 x 0 x
0 0 0 0 0 0 0 1 x 0 x
0 0 0 0 0 0 0 0 x 0 x
0 0 0 0 0 0 0 1 x 0 x
0 0 0 0 0 0 0 0 x 0 x
0 0 0 0 0 0 0 1 x 0 x
0 0 0 0 0 0 0 0 x 0 x
0 0 0 0 0 0 0 1 x 0 x
0 0 0 0 0 0 0 0 x 0 x
0 0 0 0 0 0 0 1 x 0 x
0 0 0 0 0 0 0 0 x 0 x
0 0 0 0 0 0 0 1 x 0 x
0 0 0 0 0 0 0 0 x 0 x
0 0 0 0 0 0 0 1 x 0 x
0 0 0 0 0 0 0 0 x 0 x
0 0 0 0 0 0 0 1 x 0 x
0 0 0 0 0 0 0 0 x 0 x
0 0 0 0 0 0 0 1 x 0 x
0 0 0 0 0 0 0 0 x 0 x
0 0 0 0 0 0 0 1 x 0 x
0 0 0 0 0 0 0 0 x 0 x
0 0 0 0 0 0 0 1 x 0 x
0 0 0 0 0 0 0 0 x 0 x
0 0 0 0 0 0 0 1 x 0 x
0 0 0 0 0 0 0 0 x 0 x
0 0 0 0 0 0 0 1 x 0 x
0 0 0 0 0 0 0 0 x 0 x
0 0 0 0 0 0 0 1 x 0 x
0 0 0 0 0 0 0 0 x 0 x
0 0 0 0 0 0 0 1 x 0 x
0 0 0 0 0 0 0 0 x 0 x
0 0 0 0 0 0 0 1 x 0 x
0 0 0 0 0 0 0 0 x 0 x
0 0 0 0 0 0 0 1 x 0 x
0 0 0 0 0 0 0 0 x 0 x
0 0 0 0 0 0 0 1 x 0 x
0 0 0 0 0 0 0 0 x 0 x
0 0 0 0 0 0 0 1 x 0 x
0 0 0 0 0 0 0 0 x 0 x
0 0 0 0 0 0 0 1 x 0 x
0 0 0 0 0 0 0 0 x 0 x
0 0 0 0 0 0 0 1 x 0 x
0 0 0 0 0 0 0 0 x 0 x
0 0 0 0 0 0 0 1 x 0 x
0 0 0 0 0 0 0 0 x 0 x
0 0 0 0 0 0 0 1 x 0 x
0 0 0 0 0 0 0 0 x 0 x
0 0 0 0 0 0 0 1 x 0 x
0 0 0 0 0 0 0 0 x 0 x
0 0 0 0 0 0 0 1 x 0 x
0 0 0 0 0 0 0 0 x 0 x
0 0 0 0 0 0 0 1 x 0 x
0 0 0 0 0 0 0 0 x 0 x
0 0 0 0 0 0 0 1 x 0 x
0 0 0 0 0 0 0 0 x 0 x
0 0 0 0 0 0 0 1 x 0 x
0 0 0 0 0 0 0 0 x 0 x
0 0 0 0 0 0 0 1 x 0 x
0 0 0 0 0 0 0 0 x 0 x
0 0 0 0 0 0 0 1 x 0 x
0 0 0 0 0 0 0 0 x 0 x
0 0 0 0 0 0 0 1 x 0 x
0 0 0 0 0 0 0 0 x 0 x
0 0 0 0 0 0 0 1 x 0 x
0 0 0 0 0 0 0 0 x 0 x
0 0 0 0 0 0 0 1 x 0 x
0 0 0 0 0 0 0 0 x 0 x
0 0 0 0 0 0 0 1 x 0 x
0 0 0 0 0 0 0 0 x 0 x
0 0 0 0 0 0 0 1 x 0 x
0 0 0 0 0 0 0 0 x 0 x
0 0 0 0 0 0 0 1 x 0 x
0 0 0 0 0 0 0 0 x 0 x
0 0 0 0 0 0 0 1 x 0 x
0 0 0 0 0 0 0 0 x 0 x
0 0 0 0 0 0 0 1 x 0 x
0 0 0 0 0 0 0 0 x 0 x
0 0 0 0 0 0 0 1 x 0 x
0 0 0 0 0 0 0 0 x 0 x
0 0 0 0 0 0 0 1 x 0 x
0 0 0 0 0 0 0 0 x 0 x
0 0 0 0 0 0 0 1 x 0 x
0 0 0 0 0 0 0 0 x 0 x
0 0 0 0 0 0 0 1 x 0 x
0 0 0 0 0 0 0 0 x 0 x
0 0 0 0 0 0 0 1 x 0 x
0 0 0 0 0 0 0 0 x 0 x
0 0 0 0 0 0 0 1 x 0 x
0 0 0 0 0 0 0 0 x 0 x
0 0 0 0 0 0 0 1 x 0 x
0 0 0 0 0 0 0 0 x 0 x
0 0 0 0 0 0 0 1 x 0 x
0 0 0 0 0 0 0 0 x 0 x
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*/

/* Test case 10:
M N progIN reset progLoad start result clk valid done output
0 0 0 0 0 0 0 0 x x x
0 0 0 0 0 0 0 1 x x x
0 0 0 1 0 0 0 0 x x x
0 0 0 1 0 0 0 1 0 0 x
0 0 0 0 0 0 0 0 0 0 x
0 0 0 0 0 0 0 1 0 0 x
0 0 0 0 0 0 0 0 0 0 x
0 0 0 0 0 0 0 1 0 0 x
0 0 0 0 0 0 0 0 0 0 x
0 0 0 0 0 0 0 1 0 0 x
0 0 0 0 0 0 0 0 0 0 x
0 0 0 0 0 0 0 1 0 0 x
0 0 0 0 0 0 0 0 0 0 x
0 0 0 0 0 0 0 1 0 0 x
0 0 0 0 0 0 0 0 0 0 x
0 0 0 0 0 0 0 1 0 0 x
0 0 0 0 0 0 0 0 0 0 x
0 0 0 0 0 0 0 1 0 0 x
0 0 0 0 0 0 0 0 0 0 x
0 0 0 0 0 0 0 1 0 0 x
0 0 0 0 0 0 0 0 0 0 x
0 0 0 0 0 0 0 1 0 0 x
0 0 0 0 0 0 0 0 0 0 x
0 0 0 0 0 0 0 1 0 0 x
0 0 0 0 0 0 0 0 0 0 x
0 0 0 0 0 0 0 1 0 0 x
0 0 0 0 0 0 0 0 0 0 x
0 0 0 0 0 0 0 1 0 0 x
0 0 0 0 0 0 0 0 0 0 x
0 0 0 0 0 0 0 1 0 0 x
0 0 0 0 0 0 0 0 0 0 x
0 0 0 0 0 0 0 1 0 0 x
0 0 0 0 0 0 0 0 0 0 x
0 0 0 0 0 0 0 1 0 0 x
0 0 0 0 0 0 0 0 0 0 x
0 0 0 0 0 0 0 1 0 0 x
0 0 0 0 0 0 0 0 0 0 x
0 0 0 0 0 0 0 1 0 0 x
0 0 0 0 0 0 0 0 0 0 x
0 0 0 0 0 0 0 1 0 0 x
0 0 0 0 0 0 0 0 0 0 x
0 0 0 0 0 0 0 1 0 0 x
0 0 446 0 1 0 0 0 0 0 x
0 0 446 0 1 0 0 1 0 0 x
0 0 2817 0 1 0 0 0 0 0 x
0 0 2817 0 1 0 0 1 0 0 x
0 0 426 0 1 0 0 0 0 0 x
0 0 426 0 1 0 0 1 0 0 x
0 0 2831 0 1 0 0 0 0 0 x
0 0 2831 0 1 0 0 1 0 0 x
0 0 7711 0 1 0 0 0 0 0 x
0 0 7711 0 1 0 0 1 0 0 x
0 0 7936 0 1 0 0 0 0 0 x
0 0 7936 0 1 0 0 1 0 0 x
0 0 0 0 0 0 0 0 0 0 x
0 0 0 0 0 0 0 1 0 0 x
0 0 0 0 0 0 0 0 0 0 x
0 0 0 0 0 0 0 1 0 0 x
0 0 0 0 0 0 0 0 0 0 x
0 0 0 0 0 0 0 1 0 0 x
0 0 0 0 0 1 0 0 x 0 x
0 0 0 0 0 1 0 1 x 0 x
0 0 0 0 0 0 0 0 x 0 x
0 0 0 0 0 0 0 1 x 0 x
0 0 0 0 0 0 0 0 x 0 x
0 0 0 0 0 0 0 1 x 0 x
0 0 0 0 0 0 0 0 x 0 x
0 0 0 0 0 0 0 1 x 0 x
0 0 0 0 0 0 0 0 x 0 x
0 0 0 0 0 0 0 1 x 0 x
0 0 0 0 0 0 0 0 x 0 x
0 0 0 0 0 0 0 1 x 0 x
0 0 0 0 0 0 0 0 x 0 x
0 0 0 0 0 0 0 1 x 0 x
0 0 0 0 0 0 0 0 x 0 x
0 0 0 0 0 0 0 1 x 0 x
0 0 0 0 0 0 0 0 x 0 x
0 0 0 0 0 0 0 1 x 0 x
0 0 0 0 0 0 0 0 x 0 x
0 0 0 0 0 0 0 1 x 0 x
0 0 0 0 0 0 0 0 x 0 x
0 0 0 0 0 0 0 1 x 0 x
0 0 0 0 0 0 0 0 x 0 x
0 0 0 0 0 0 0 1 x 0 x
0 0 0 0 0 0 0 0 x 0 x
0 0 0 0 0 0 0 1 x 0 x
0 0 0 0 0 0 0 0 x 0 x
0 0 0 0 0 0 0 1 x 0 x
0 0 0 0 0 0 0 0 x 0 x
0 0 0 0 0 0 0 1 x 0 x
0 0 0 0 0 0 0 0 x 0 x
0 0 0 0 0 0 0 1 x 0 x
0 0 0 0 0 0 0 0 x 0 x
0 0 0 0 0 0 0 1 x 0 x
0 0 0 0 0 0 0 0 x 0 x
0 0 0 0 0 0 0 1 x 0 x
0 0 0 0 0 0 0 0 x 0 x
0 0 0 0 0 0 0 1 x 0 x
0 0 0 0 0 0 0 0 x 0 x
0 0 0 0 0 0 0 1 x 0 x
0 0 0 0 0 0 0 0 x 0 x
0 0 0 0 0 0 0 1 x 0 x
0 0 0 0 0 0 0 0 x 0 x
0 0 0 0 0 0 0 1 x 0 x
0 0 0 0 0 0 0 0 x 0 x
0 0 0 0 0 0 0 1 x 0 x
0 0 0 0 0 0 0 0 x 0 x
0 0 0 0 0 0 0 1 x 0 x
0 0 0 0 0 0 0 0 x 0 x
0 0 0 0 0 0 0 1 x 0 x
0 0 0 0 0 0 0 0 x 0 x
0 0 0 0 0 0 0 1 x 0 x
0 0 0 0 0 0 0 0 x 0 x
0 0 0 0 0 0 0 1 x 0 x
0 0 0 0 0 0 0 0 x 0 x
0 0 0 0 0 0 0 1 x 0 x
0 0 0 0 0 0 0 0 x 0 x
0 0 0 0 0 0 0 1 x 0 x
0 0 0 0 0 0 0 0 x 0 x
0 0 0 0 0 0 0 1 x 0 x
0 0 0 0 0 0 0 0 x 0 x
0 0 0 0 0 0 0 1 x 0 x
0 0 0 0 0 0 0 0 x 0 x
0 0 0 0 0 0 0 1 x 0 x
0 0 0 0 0 0 0 0 x 0 x
0 0 0 0 0 0 0 1 x 0 x
0 0 0 0 0 0 0 0 x 0 x
0 0 0 0 0 0 0 1 x 0 x
0 0 0 0 0 0 0 0 x 0 x
0 0 0 0 0 0 0 1 x 0 x
0 0 0 0 0 0 0 0 x 0 x
0 0 0 0 0 0 0 1 x 0 x
0 0 0 0 0 0 0 0 x 0 x
0 0 0 0 0 0 0 1 x 0 x
0 0 0 0 0 0 0 0 x 0 x
0 0 0 0 0 0 0 1 x 0 x
0 0 0 0 0 0 0 0 x 0 x
0 0 0 0 0 0 0 1 x 0 x
0 0 0 0 0 0 0 0 x 0 x
0 0 0 0 0 0 0 1 x 0 x
0 0 0 0 0 0 0 0 x 0 x
0 0 0 0 0 0 0 1 x 0 x
0 0 0 0 0 0 0 0 x 0 x
0 0 0 0 0 0 0 1 x 0 x
0 0 0 0 0 0 0 0 x 0 x
0 0 0 0 0 0 0 1 x 0 x
0 0 0 0 0 0 0 0 x 0 x
0 0 0 0 0 0 0 1 x 0 x
0 0 0 0 0 0 0 0 x 0 x
0 0 0 0 0 0 0 1 x 0 x
0 0 0 0 0 0 0 0 x 0 x
0 0 0 0 0 0 0 1 x 0 x
0 0 0 0 0 0 0 0 x 0 x
0 0 0 0 0 0 0 1 x 0 x
0 0 0 0 0 0 0 0 x 0 x
0 0 0 0 0 0 0 1 x 0 x
0 0 0 0 0 0 0 0 x 0 x
0 0 0 0 0 0 0 1 x 0 x
0 0 0 0 0 0 0 0 x 0 x
0 0 0 0 0 0 0 1 x 0 x
0 0 0 0 0 0 0 0 x 0 x
0 0 0 0 0 0 0 1 x 0 x
0 0 0 0 0 0 0 0 x 0 x
0 0 0 0 0 0 0 1 x 0 x
0 0 0 0 0 0 0 0 x 0 x
0 0 0 0 0 0 0 1 x 0 x
0 0 0 0 0 0 0 0 x 0 x
0 0 0 0 0 0 0 1 x 0 x
0 0 0 0 0 0 0 0 x 0 x
0 0 0 0 0 0 0 1 x 0 x
0 0 0 0 0 0 0 0 x 0 x
0 0 0 0 0 0 0 1 x 0 x
0 0 0 0 0 0 0 0 x 0 x
0 0 0 0 0 0 0 1 x 0 x
0 0 0 0 0 0 0 0 x 0 x
0 0 0 0 0 0 0 1 x 0 x
0 0 0 0 0 0 0 0 x 0 x
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*/

/* Test case 11:
M N progIN reset progLoad start result clk valid done output
0 0 0 0 0 0 0 0 x x x
0 0 0 0 0 0 0 1 x x x
0 0 0 1 0 0 0 0 x x x
0 0 0 1 0 0 0 1 0 0 x
0 0 0 0 0 0 0 0 0 0 x
0 0 0 0 0 0 0 1 0 0 x
0 0 0 0 0 0 0 0 0 0 x
0 0 0 0 0 0 0 1 0 0 x
0 0 0 0 0 0 0 0 0 0 x
0 0 0 0 0 0 0 1 0 0 x
0 0 0 0 0 0 0 0 0 0 x
0 0 0 0 0 0 0 1 0 0 x
0 0 0 0 0 0 0 0 0 0 x
0 0 0 0 0 0 0 1 0 0 x
0 0 0 0 0 0 0 0 0 0 x
0 0 0 0 0 0 0 1 0 0 x
0 0 0 0 0 0 0 0 0 0 x
0 0 0 0 0 0 0 1 0 0 x
0 0 0 0 0 0 0 0 0 0 x
0 0 0 0 0 0 0 1 0 0 x
0 0 0 0 0 0 0 0 0 0 x
0 0 0 0 0 0 0 1 0 0 x
0 0 0 0 0 0 0 0 0 0 x
0 0 0 0 0 0 0 1 0 0 x
0 0 0 0 0 0 0 0 0 0 x
0 0 0 0 0 0 0 1 0 0 x
0 0 0 0 0 0 0 0 0 0 x
0 0 0 0 0 0 0 1 0 0 x
0 0 0 0 0 0 0 0 0 0 x
0 0 0 0 0 0 0 1 0 0 x
0 0 0 0 0 0 0 0 0 0 x
0 0 0 0 0 0 0 1 0 0 x
0 0 0 0 0 0 0 0 0 0 x
0 0 0 0 0 0 0 1 0 0 x
0 0 0 0 0 0 0 0 0 0 x
0 0 0 0 0 0 0 1 0 0 x
0 0 0 0 0 0 0 0 0 0 x
0 0 0 0 0 0 0 1 0 0 x
0 0 0 0 0 0 0 0 0 0 x
0 0 0 0 0 0 0 1 0 0 x
0 0 0 0 0 0 0 0 0 0 x
0 0 0 0 0 0 0 1 0 0 x
0 0 5 0 1 0 0 0 0 0 x
0 0 5 0 1 0 0 1 0 0 x
0 0 47 0 1 0 0 0 0 0 x
0 0 47 0 1 0 0 1 0 0 x
0 0 2304 0 1 0 0 0 0 0 x
0 0 2304 0 1 0 0 1 0 0 x
0 0 2816 0 1 0 0 0 0 0 x
0 0 2816 0 1 0 0 1 0 0 x
0 0 2305 0 1 0 0 0 0 0 x
0 0 2305 0 1 0 0 1 0 0 x
0 0 2817 0 1 0 0 0 0 0 x
0 0 2817 0 1 0 0 1 0 0 x
0 0 1024 0 1 0 0 0 0 0 x
0 0 1024 0 1 0 0 1 0 0 x
0 0 2304 0 1 0 0 0 0 0 x
0 0 2304 0 1 0 0 1 0 0 x
0 0 4352 0 1 0 0 0 0 0 x
0 0 4352 0 1 0 0 1 0 0 x
0 0 2818 0 1 0 0 0 0 0 x
0 0 2818 0 1 0 0 1 0 0 x
0 0 2304 0 1 0 0 0 0 0 x
0 0 2304 0 1 0 0 1 0 0 x
0 0 4608 0 1 0 0 0 0 0 x
0 0 4608 0 1 0 0 1 0 0 x
0 0 2819 0 1 0 0 0 0 0 x
0 0 2819 0 1 0 0 1 0 0 x
0 0 2304 0 1 0 0 0 0 0 x
0 0 2304 0 1 0 0 1 0 0 x
0 0 4864 0 1 0 0 0 0 0 x
0 0 4864 0 1 0 0 1 0 0 x
0 0 2820 0 1 0 0 0 0 0 x
0 0 2820 0 1 0 0 1 0 0 x
0 0 2304 0 1 0 0 0 0 0 x
0 0 2304 0 1 0 0 1 0 0 x
0 0 5120 0 1 0 0 0 0 0 x
0 0 5120 0 1 0 0 1 0 0 x
0 0 2821 0 1 0 0 0 0 0 x
0 0 2821 0 1 0 0 1 0 0 x
0 0 2304 0 1 0 0 0 0 0 x
0 0 2304 0 1 0 0 1 0 0 x
0 0 5376 0 1 0 0 0 0 0 x
0 0 5376 0 1 0 0 1 0 0 x
0 0 2822 0 1 0 0 0 0 0 x
0 0 2822 0 1 0 0 1 0 0 x
0 0 2304 0 1 0 0 0 0 0 x
0 0 2304 0 1 0 0 1 0 0 x
0 0 5632 0 1 0 0 0 0 0 x
0 0 5632 0 1 0 0 1 0 0 x
0 0 2823 0 1 0 0 0 0 0 x
0 0 2823 0 1 0 0 1 0 0 x
0 0 7936 0 1 0 0 0 0 0 x
0 0 7936 0 1 0 0 1 0 0 x
0 0 0 0 0 1 0 0 0 0 x
0 0 0 0 0 1 0 1 0 0 x
0 0 0 0 0 0 0 0 x 0 x
0 0 0 0 0 0 0 1 x 0 x
0 0 0 0 0 0 0 0 x 0 x
0 0 0 0 0 0 0 1 x 0 x
0 0 0 0 0 0 0 0 x 0 x
0 0 0 0 0 0 0 1 x 0 x
0 0 0 0 0 0 0 0 x 0 x
0 0 0 0 0 0 0 1 x 0 x
0 0 0 0 0 0 0 0 x 0 x
0 0 0 0 0 0 0 1 x 0 x
0 0 0 0 0 0 0 0 x 0 x
0 0 0 0 0 0 0 1 x 0 x
0 0 0 0 0 0 0 0 x 0 x
0 0 0 0 0 0 0 1 x 0 x
0 0 0 0 0 0 0 0 x 0 x
0 0 0 0 0 0 0 1 x 0 x
0 0 0 0 0 0 0 0 x 0 x
0 0 0 0 0 0 0 1 x 0 x
0 0 0 0 0 0 0 0 x 0 x
0 0 0 0 0 0 0 1 x 0 x
0 0 0 0 0 0 0 0 x 0 x
0 0 0 0 0 0 0 1 x 0 x
0 0 0 0 0 0 0 0 x 0 x
0 0 0 0 0 0 0 1 x 0 x
0 0 0 0 0 0 0 0 x 0 x
0 0 0 0 0 0 0 1 x 0 x
0 0 0 0 0 0 0 0 x 0 x
0 0 0 0 0 0 0 1 x 0 x
0 0 0 0 0 0 0 0 x 0 x
0 0 0 0 0 0 0 1 x 0 x
0 0 0 0 0 0 0 0 x 0 x
0 0 0 0 0 0 0 1 x 0 x
0 0 0 0 0 0 0 0 x 0 x
0 0 0 0 0 0 0 1 x 0 x
0 0 0 0 0 0 0 0 x 0 x
0 0 0 0 0 0 0 1 x 0 x
0 0 0 0 0 0 0 0 x 0 x
0 0 0 0 0 0 0 1 x 0 x
0 0 0 0 0 0 0 0 x 0 x
0 0 0 0 0 0 0 1 x 0 x
0 0 0 0 0 0 0 0 x 0 x
0 0 0 0 0 0 0 1 x 0 x
0 0 0 0 0 0 0 0 x 0 x
0 0 0 0 0 0 0 1 x 0 x
0 0 0 0 0 0 0 0 x 0 x
0 0 0 0 0 0 0 1 x 0 x
0 0 0 0 0 0 0 0 x 0 x
0 0 0 0 0 0 0 1 x 0 x
0 0 0 0 0 0 0 0 x 0 x
0 0 0 0 0 0 0 1 x 0 x
0 0 0 0 0 0 0 0 x 0 x
0 0 0 0 0 0 0 1 x 0 x
0 0 0 0 0 0 0 0 x 0 x
0 0 0 0 0 0 0 1 x 0 x
0 0 0 0 0 0 0 0 x 0 x
0 0 0 0 0 0 0 1 x 0 x
0 0 0 0 0 0 0 0 x 0 x
0 0 0 0 0 0 0 1 x 0 x
0 0 0 0 0 0 0 0 x 0 x
0 0 0 0 0 0 0 1 x 0 x
0 0 0 0 0 0 0 0 x 0 x
0 0 0 0 0 0 0 1 x 0 x
0 0 0 0 0 0 0 0 x 0 x
0 0 0 0 0 0 0 1 x 0 x
0 0 0 0 0 0 0 0 x 0 x
0 0 0 0 0 0 0 1 x 0 x
0 0 0 0 0 0 0 0 x 0 x
0 0 0 0 0 0 0 1 x 0 x
0 0 0 0 0 0 0 0 x 0 x
0 0 0 0 0 0 0 1 x 0 x
0 0 0 0 0 0 0 0 x 0 x
0 0 0 0 0 0 0 1 x 0 x
0 0 0 0 0 0 0 0 x 0 x
0 0 0 0 0 0 0 1 x 0 x
0 0 0 0 0 0 0 0 x 0 x
0 0 0 0 0 0 0 1 x 0 x
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*/

/* Test case 12:
M N progIN reset progLoad start result clk valid done output
0 0 0 0 0 0 0 0 x x x
0 0 0 0 0 0 0 1 x x x
0 0 0 1 0 0 0 0 x x x
0 0 0 1 0 0 0 1 0 0 x
0 0 0 0 0 0 0 0 0 0 x
0 0 0 0 0 0 0 1 0 0 x
0 0 0 0 0 0 0 0 0 0 x
0 0 0 0 0 0 0 1 0 0 x
0 0 0 0 0 0 0 0 0 0 x
0 0 0 0 0 0 0 1 0 0 x
0 0 0 0 0 0 0 0 0 0 x
0 0 0 0 0 0 0 1 0 0 x
0 0 0 0 0 0 0 0 0 0 x
0 0 0 0 0 0 0 1 0 0 x
0 0 0 0 0 0 0 0 0 0 x
0 0 0 0 0 0 0 1 0 0 x
0 0 0 0 0 0 0 0 0 0 x
0 0 0 0 0 0 0 1 0 0 x
0 0 0 0 0 0 0 0 0 0 x
0 0 0 0 0 0 0 1 0 0 x
0 0 0 0 0 0 0 0 0 0 x
0 0 0 0 0 0 0 1 0 0 x
0 0 0 0 0 0 0 0 0 0 x
0 0 0 0 0 0 0 1 0 0 x
0 0 0 0 0 0 0 0 0 0 x
0 0 0 0 0 0 0 1 0 0 x
0 0 0 0 0 0 0 0 0 0 x
0 0 0 0 0 0 0 1 0 0 x
0 0 0 0 0 0 0 0 0 0 x
0 0 0 0 0 0 0 1 0 0 x
0 0 0 0 0 0 0 0 0 0 x
0 0 0 0 0 0 0 1 0 0 x
0 0 0 0 0 0 0 0 0 0 x
0 0 0 0 0 0 0 1 0 0 x
0 0 0 0 0 0 0 0 0 0 x
0 0 0 0 0 0 0 1 0 0 x
0 0 0 0 0 0 0 0 0 0 x
0 0 0 0 0 0 0 1 0 0 x
0 0 0 0 0 0 0 0 0 0 x
0 0 0 0 0 0 0 1 0 0 x
0 0 0 0 0 0 0 0 0 0 x
0 0 0 0 0 0 0 1 0 0 x
0 0 5 0 1 0 0 0 0 0 x
0 0 5 0 1 0 0 1 0 0 x
0 0 47 0 1 0 0 0 0 0 x
0 0 47 0 1 0 0 1 0 0 x
0 0 2304 0 1 0 0 0 0 0 x
0 0 2304 0 1 0 0 1 0 0 x
0 0 2816 0 1 0 0 0 0 0 x
0 0 2816 0 1 0 0 1 0 0 x
0 0 2305 0 1 0 0 0 0 0 x
0 0 2305 0 1 0 0 1 0 0 x
0 0 2817 0 1 0 0 0 0 0 x
0 0 2817 0 1 0 0 1 0 0 x
0 0 1024 0 1 0 0 0 0 0 x
0 0 1024 0 1 0 0 1 0 0 x
0 0 2304 0 1 0 0 0 0 0 x
0 0 2304 0 1 0 0 1 0 0 x
0 0 4352 0 1 0 0 0 0 0 x
0 0 4352 0 1 0 0 1 0 0 x
0 0 2818 0 1 0 0 0 0 0 x
0 0 2818 0 1 0 0 1 0 0 x
0 0 2304 0 1 0 0 0 0 0 x
0 0 2304 0 1 0 0 1 0 0 x
0 0 4608 0 1 0 0 0 0 0 x
0 0 4608 0 1 0 0 1 0 0 x
0 0 2819 0 1 0 0 0 0 0 x
0 0 2819 0 1 0 0 1 0 0 x
0 0 2304 0 1 0 0 0 0 0 x
0 0 2304 0 1 0 0 1 0 0 x
0 0 4864 0 1 0 0 0 0 0 x
0 0 4864 0 1 0 0 1 0 0 x
0 0 2820 0 1 0 0 0 0 0 x
0 0 2820 0 1 0 0 1 0 0 x
0 0 2304 0 1 0 0 0 0 0 x
0 0 2304 0 1 0 0 1 0 0 x
0 0 5120 0 1 0 0 0 0 0 x
0 0 5120 0 1 0 0 1 0 0 x
0 0 2821 0 1 0 0 0 0 0 x
0 0 2821 0 1 0 0 1 0 0 x
0 0 2304 0 1 0 0 0 0 0 x
0 0 2304 0 1 0 0 1 0 0 x
0 0 5376 0 1 0 0 0 0 0 x
0 0 5376 0 1 0 0 1 0 0 x
0 0 2822 0 1 0 0 0 0 0 x
0 0 2822 0 1 0 0 1 0 0 x
0 0 2304 0 1 0 0 0 0 0 x
0 0 2304 0 1 0 0 1 0 0 x
0 0 5632 0 1 0 0 0 0 0 x
0 0 5632 0 1 0 0 1 0 0 x
0 0 2823 0 1 0 0 0 0 0 x
0 0 2823 0 1 0 0 1 0 0 x
0 0 7936 0 1 0 0 0 0 0 x
0 0 7936 0 1 0 0 1 0 0 x
0 0 0 0 0 1 0 0 0 0 x
0 0 0 0 0 1 0 1 0 0 x
0 0 0 0 0 0 0 0 x 0 x
0 0 0 0 0 0 0 1 x 0 x
0 0 0 0 0 0 0 0 x 0 x
0 0 0 0 0 0 0 1 x 0 x
0 0 0 0 0 0 0 0 x 0 x
0 0 0 0 0 0 0 1 x 0 x
0 0 0 0 0 0 0 0 x 0 x
0 0 0 0 0 0 0 1 x 0 x
0 0 0 0 0 0 0 0 x 0 x
0 0 0 0 0 0 0 1 x 0 x
0 0 0 0 0 0 0 0 x 0 x
0 0 0 0 0 0 0 1 x 0 x
0 0 0 0 0 0 0 0 x 0 x
0 0 0 0 0 0 0 1 x 0 x
0 0 0 0 0 0 0 0 x 0 x
0 0 0 0 0 0 0 1 x 0 x
0 0 0 0 0 0 0 0 x 0 x
0 0 0 0 0 0 0 1 x 0 x
0 0 0 0 0 0 0 0 x 0 x
0 0 0 0 0 0 0 1 x 0 x
0 0 0 0 0 0 0 0 x 0 x
0 0 0 0 0 0 0 1 x 0 x
0 0 0 0 0 0 0 0 x 0 x
0 0 0 0 0 0 0 1 x 0 x
0 0 0 0 0 0 0 0 x 0 x
0 0 0 0 0 0 0 1 x 0 x
0 0 0 0 0 0 0 0 x 0 x
0 0 0 0 0 0 0 1 x 0 x
0 0 0 0 0 0 0 0 x 0 x
0 0 0 0 0 0 0 1 x 0 x
0 0 0 0 0 0 0 0 x 0 x
0 0 0 0 0 0 0 1 x 0 x
0 0 0 0 0 0 0 0 x 0 x
0 0 0 0 0 0 0 1 x 0 x
0 0 0 0 0 0 0 0 x 0 x
0 0 0 0 0 0 0 1 x 0 x
0 0 0 0 0 0 0 0 x 0 x
0 0 0 0 0 0 0 1 x 0 x
0 0 0 0 0 0 0 0 x 0 x
0 0 0 0 0 0 0 1 x 0 x
0 0 0 0 0 0 0 0 x 0 x
0 0 0 0 0 0 0 1 x 0 x
0 0 0 0 0 0 0 0 x 0 x
0 0 0 0 0 0 0 1 x 0 x
0 0 0 0 0 0 0 0 x 0 x
0 0 0 0 0 0 0 1 x 0 x
0 0 0 0 0 0 0 0 x 0 x
0 0 0 0 0 0 0 1 x 0 x
0 0 0 0 0 0 0 0 x 0 x
0 0 0 0 0 0 0 1 x 0 x
0 0 0 0 0 0 0 0 x 0 x
0 0 0 0 0 0 0 1 x 0 x
0 0 0 0 0 0 0 0 x 0 x
0 0 0 0 0 0 0 1 x 0 x
0 0 0 0 0 0 0 0 x 0 x
0 0 0 0 0 0 0 1 x 0 x
0 0 0 0 0 0 0 0 x 0 x
0 0 0 0 0 0 0 1 x 0 x
0 0 0 0 0 0 0 0 x 0 x
0 0 0 0 0 0 0 1 x 0 x
0 0 0 0 0 0 0 0 x 0 x
0 0 0 0 0 0 0 1 x 0 x
0 0 0 0 0 0 0 0 x 0 x
0 0 0 0 0 0 0 1 x 0 x
0 0 0 0 0 0 0 0 x 0 x
0 0 0 0 0 0 0 1 x 0 x
0 0 0 0 0 0 0 0 x 0 x
0 0 0 0 0 0 0 1 x 0 x
0 0 0 0 0 0 0 0 x 0 x
0 0 0 0 0 0 0 1 x 0 x
0 0 0 0 0 0 0 0 x 0 x
0 0 0 0 0 0 0 1 x 0 x
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*/

/* Test case 13:
M N progIN reset progLoad start result clk valid done output
0 0 0 0 0 0 0 0 x x x
0 0 0 0 0 0 0 1 x x x
0 0 0 1 0 0 0 0 x x x
0 0 0 1 0 0 0 1 0 0 x
0 0 0 0 0 0 0 0 0 0 x
0 0 0 0 0 0 0 1 0 0 x
0 0 0 0 0 0 0 0 0 0 x
0 0 0 0 0 0 0 1 0 0 x
0 0 0 0 0 0 0 0 0 0 x
0 0 0 0 0 0 0 1 0 0 x
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*/

/* Test case 14:
M N progIN reset progLoad start result clk valid done output
0 0 0 0 0 0 0 0 x x x
0 0 0 0 0 0 0 1 x x x
0 0 0 1 0 0 0 0 x x x
0 0 0 1 0 0 0 1 0 0 x
0 0 0 0 0 0 0 0 0 0 x
0 0 0 0 0 0 0 1 0 0 x
0 0 0 0 0 0 0 0 0 0 x
0 0 0 0 0 0 0 1 0 0 x
0 0 0 0 0 0 0 0 0 0 x
0 0 0 0 0 0 0 1 0 0 x
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*/

/* Test case 15:
M N progIN reset progLoad start result clk valid done output
0 0 0 0 0 0 0 0 x x x
0 0 0 0 0 0 0 1 x x x
0 0 0 1 0 0 0 0 x x x
0 0 0 1 0 0 0 1 0 0 x
0 0 0 0 0 0 0 0 0 0 x
0 0 0 0 0 0 0 1 0 0 x
0 0 0 0 0 0 0 0 0 0 x
0 0 0 0 0 0 0 1 0 0 x
0 0 0 0 0 0 0 0 0 0 x
0 0 0 0 0 0 0 1 0 0 x
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*/

/* Test case And:
M N progIN reset progLoad start result clk valid done output
0 0 0 0 0 0 0 0 0 0 0
0 0 0 0 0 0 0 1 0 0 0
0 0 0 1 0 0 0 0 0 0 0
0 0 0 1 0 0 0 1 0 0 0
0 0 0 0 0 0 0 0 0 0 0
0 0 0 0 0 0 0 1 0 0 0
0 0 0 0 0 0 0 0 0 0 0
0 0 0 0 0 0 0 1 0 0 0
0 0 0 0 0 0 0 0 0 0 0
0 0 0 0 0 0 0 1 0 0 0
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*/

/* Test case 01_P01T01:
M N progIN reset progLoad start result clk valid done output
0 0 0 0 0 0 0 0 0 0 0
0 0 0 0 0 0 0 1 0 0 0
0 0 0 1 0 0 0 0 0 0 0
0 0 0 1 0 0 0 1 0 0 0
0 0 0 0 0 0 0 0 0 0 0
0 0 0 0 0 0 0 1 0 0 0
0 0 0 0 0 0 0 0 0 0 0
0 0 0 0 0 0 0 1 0 0 0
0 0 0 0 0 0 0 0 0 0 0
0 0 0 0 0 0 0 1 0 0 0
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*/

/* Test case 02_P01T02:
M N progIN reset progLoad start result clk valid done output
0 0 0 0 0 0 0 0 x x x
0 0 0 0 0 0 0 1 x x x
0 0 0 1 0 0 0 0 x x x
0 0 0 1 0 0 0 1 0 0 0
0 0 0 0 0 0 0 0 0 0 0
0 0 0 0 0 0 0 1 0 0 0
0 0 0 0 0 0 0 0 0 0 0
0 0 0 0 0 0 0 1 0 0 0
0 0 0 0 0 0 0 0 0 0 0
0 0 0 0 0 0 0 1 0 0 0
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*/

/* Test case OR:
M N progIN reset progLoad start result clk valid done output
0 0 0 0 0 0 0 0 0 0 0
0 0 0 0 0 0 0 1 0 0 0
0 0 0 1 0 0 0 0 0 0 0
0 0 0 1 0 0 0 1 0 0 0
0 0 0 0 0 0 0 0 0 0 0
0 0 0 0 0 0 0 1 0 0 0
0 0 0 0 0 0 0 0 0 0 0
0 0 0 0 0 0 0 1 0 0 0
0 0 0 0 0 0 0 0 0 0 0
0 0 0 0 0 0 0 1 0 0 0
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*/

/* Test case 01_P01T2:
M N progIN reset progLoad start result clk valid done output
0 0 0 0 0 0 0 0 x x x
0 0 0 0 0 0 0 1 x x x
0 0 0 1 0 0 0 0 x x x
0 0 0 1 0 0 0 1 0 0 0
0 0 0 0 0 0 0 0 0 0 0
0 0 0 0 0 0 0 1 0 0 0
0 0 0 0 0 0 0 0 0 0 0
0 0 0 0 0 0 0 1 0 0 0
0 0 0 0 0 0 0 0 0 0 0
0 0 0 0 0 0 0 1 0 0 0
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*/

/* Test case 02_P01T3:
M N progIN reset progLoad start result clk valid done output
0 0 0 0 0 0 0 0 x x x
0 0 0 0 0 0 0 1 x x x
0 0 0 1 0 0 0 0 x x x
0 0 0 1 0 0 0 1 0 0 x
0 0 0 0 0 0 0 0 0 0 x
0 0 0 0 0 0 0 1 0 0 x
0 0 0 0 0 0 0 0 0 0 x
0 0 0 0 0 0 0 1 0 0 x
0 0 0 0 0 0 0 0 0 0 x
0 0 0 0 0 0 0 1 0 0 x
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*/

/* Test case Xor:
M N progIN reset progLoad start result clk valid done output
0 0 0 0 0 0 0 0 0 0 0
0 0 0 0 0 0 0 1 0 0 0
0 0 0 1 0 0 0 0 0 0 0
0 0 0 1 0 0 0 1 0 0 0
0 0 0 0 0 0 0 0 0 0 0
0 0 0 0 0 0 0 1 0 0 0
0 0 0 0 0 0 0 0 0 0 0
0 0 0 0 0 0 0 1 0 0 0
0 0 0 0 0 0 0 0 0 0 0
0 0 0 0 0 0 0 1 0 0 0
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*/

/* Test case 01_P01T3:
M N progIN reset progLoad start result clk valid done output
0 0 0 0 0 0 0 0 x x x
0 0 0 0 0 0 0 1 x x x
0 0 0 1 0 0 0 0 x x x
0 0 0 1 0 0 0 1 0 0 x
0 0 0 0 0 0 0 0 0 0 x
0 0 0 0 0 0 0 1 0 0 x
0 0 0 0 0 0 0 0 0 0 x
0 0 0 0 0 0 0 1 0 0 x
0 0 0 0 0 0 0 0 0 0 x
0 0 0 0 0 0 0 1 0 0 x
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*/

/* Test case 03_P02T01:
M N progIN reset progLoad start result clk valid done output
0 0 0 0 0 0 0 0 x x x
0 0 0 0 0 0 0 1 x x x
0 0 0 1 0 0 0 0 x x x
0 0 0 1 0 0 0 1 0 0 0
0 0 0 0 0 0 0 0 0 0 0
0 0 0 0 0 0 0 1 0 0 0
0 0 0 0 0 0 0 0 0 0 0
0 0 0 0 0 0 0 1 0 0 0
0 0 0 0 0 0 0 0 0 0 0
0 0 0 0 0 0 0 1 0 0 0
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*/

/* Test case 01_P01T4:
M N progIN reset progLoad start result clk valid done output
0 0 0 0 0 0 0 0 x x x
0 0 0 0 0 0 0 1 x x x
0 0 0 1 0 0 0 0 x x x
0 0 0 1 0 0 0 1 0 0 x
0 0 0 0 0 0 0 0 0 0 x
0 0 0 0 0 0 0 1 0 0 x
0 0 0 0 0 0 0 0 0 0 x
0 0 0 0 0 0 0 1 0 0 x
0 0 0 0 0 0 0 0 0 0 x
0 0 0 0 0 0 0 1 0 0 x
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*/

/* Test case 03_P02T2:
M N progIN reset progLoad start result clk valid done output
0 0 0 0 0 0 0 0 x x x
0 0 0 0 0 0 0 1 x x x
0 0 0 1 0 0 0 0 x x x
0 0 0 1 0 0 0 1 0 0 x
0 0 0 0 0 0 0 0 0 0 x
0 0 0 0 0 0 0 1 0 0 x
0 0 0 0 0 0 0 0 0 0 x
0 0 0 0 0 0 0 1 0 0 x
0 0 0 0 0 0 0 0 0 0 x
0 0 0 0 0 0 0 1 0 0 x
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*/

/* Test case 01_P01T5:
M N progIN reset progLoad start result clk valid done output
0 0 0 0 0 0 0 0 x x x
0 0 0 0 0 0 0 1 x x x
0 0 0 1 0 0 0 0 x x x
0 0 0 1 0 0 0 1 0 0 x
0 0 0 0 0 0 0 0 0 0 x
0 0 0 0 0 0 0 1 0 0 x
0 0 0 0 0 0 0 0 0 0 x
0 0 0 0 0 0 0 1 0 0 x
0 0 0 0 0 0 0 0 0 0 x
0 0 0 0 0 0 0 1 0 0 x
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*/
